# Fritzing sketch LedChaser (saved by Fritzing 0.7.7b)
breadboards: 1

parts:
  Arduino1 = Arduino
  LED1 = LED - 5mm [color="Red (633nm)" package="5 mm [THT]"]
  LED2 = LED - 5mm [color="Red (633nm)" package="5 mm [THT]"]
  LED5 = LED - 5mm [color="Yellow (595nm)" package="5 mm [THT]"]
  LED4 = LED - 5mm [color="Yellow (595nm)" package="5 mm [THT]"]
  LED7 = LED - 5mm [color="Green (570nm)" package="5 mm [THT]"]
  LED6 = LED - 5mm [color="Green (570nm)" package="5 mm [THT]"]
  LED3 = LED - 5mm [color="Red (633nm)" package="5 mm [THT]"]
  R7 = Resistor [tolerance=±5% resistance=220 package=THT]
  R6 = Resistor [tolerance=±5% resistance=220 package=THT]
  R5 = Resistor [tolerance=±5% resistance=220 package=THT]
  R4 = Resistor [tolerance=±5% resistance=220 package=THT]
  R3 = Resistor [tolerance=±5% resistance=220 package=THT]
  R2 = Resistor [tolerance=±5% resistance=220 package=THT]
  R1 = Resistor [tolerance=±5% resistance=220 package=THT]
  S1 = Tilt Switch [package=THT]
  R8 = Resistor [tolerance=±5% resistance=10k package=THT]

nets:
  N1: Arduino1.GND, R7.Pin_1, R6.Pin_1, R5.Pin_1, R4.Pin_1, R3.Pin_1, R2.Pin_1, R1.Pin_1, R8.Pin_1
  N2: Arduino1.D10, S1.Pin_2, R8.Pin_0
  N3: Arduino1.D8, LED7.anode
  N4: Arduino1.D7, LED6.anode
  N5: Arduino1.D6, LED5.anode
  N6: Arduino1.D5, LED4.anode
  N7: Arduino1.D4, LED3.anode
  N8: Arduino1.D3, LED2.anode
  N9: Arduino1.D2, LED1.anode
  N10: Arduino1.+5V, S1.Pin_1
  N11: LED1.cathode, R1.Pin_0
  N12: LED2.cathode, R2.Pin_0
  N13: LED5.cathode, R5.Pin_0
  N14: LED4.cathode, R4.Pin_0
  N15: LED7.cathode, R7.Pin_0
  N16: LED6.cathode, R6.Pin_0
  N17: LED3.cathode, R3.Pin_0
